// Logisim project Aula 1.circ as structural Verilog: 1 circuit, main circuit main
module main (
  input  A,
  input  B,
  input  C,
  input  D,
  input  A_2,
  input  B_2,
  input  C_2,
  input  D_2,
  input  E,
  input  F
);

  wire and_1_out, and_2_out, and_3_out, not_1_out, not_2_out, or_1_out, or_2_out, S4_out, S5_out;

  and and_1 (and_1_out, A, B);
  or or_1 (or_1_out, C, D);
  and and_2 (and_2_out, A_2, B_2);
  not not_1 (not_1_out, C_2);
  or or_2 (or_2_out, D_2, E);
  not not_2 (not_2_out, F);
  LED led_1 (.in(and_3_out));
  and and_3 (and_3_out, and_1_out, or_1_out);
  or S4 (S4_out, and_2_out, not_1_out, or_2_out);
  and S5 (S5_out, S4_out, not_2_out);
  LED led_2 (.in(S5_out));

  // Notes on the sheet:
  //   S1=A*B
  //   S2=A+B
  //   S1
  //   S2
  //   S3
  //   S4
  //   S=S1+S2
endmodule
