// Logisim project Aula2-Ex2(n2).circ as structural Verilog: 1 circuit, main circuit main
module main (
  input  A,
  input  B,
  input  C,
  input  D,
  input  E,
  input  F
);

  wire and_1_out, and_2_out, or_1_out;

  and and_1 (and_1_out, A, C);
  or or_1 (or_1_out, B, D);
  and and_2 (and_2_out, E, F);
  // OR_Gate or_2 has open pins: in0=and_1_out, in2=or_1_out, in4=and_2_out, out=open
endmodule
